# Fritzing sketch Water Tank Level Sensor G1 (saved by Fritzing 0.9.2b)
breadboards: 1

parts:
  Part1 = Arduino Uno (Rev3)
  R1 = Rotary Potentiometer (Small) [maximum_resistance=100kΩ package=THT]
  S1 = Pushbutton [package="[THT]"]
  R2 = Resistor [tolerance=±5% resistance=220 package=THT]
  LCD1 = LCD screen
  Part2 = SRF05 Ultrasonic Rangefinder
  LED1 = LED - 5mm [color="Red (633nm)" package="5 mm [THT]"]
  R3 = Resistor [tolerance=±5% resistance=220 package=THT]

nets:
  N1: Part1.D8, Part2.Trig
  N2: Part1.D9_PWM, Part2.Echo
  N3: Part1.D13/SCK, LED1.anode
  GND: Part1.GND, S1.Pin_3, S1.Pin_4, LCD1.VSS, LCD1.V0, LCD1.R/W, LCD1.LED-, Part2.GND, R3.Pin_0
  N4: Part1.D2, LCD1.DB7
  N5: Part1.D3_PWM, LCD1.DB6
  N6: Part1.D4, LCD1.DB5
  N7: Part1.D5_PWM, LCD1.DB4
  N8: Part1.RESET, S1.Pin_1, S1.Pin_2
  N9: R1.leg1, R2.Pin_1
  N10: R1.wiper, LCD1.LED+
  VDD: R2.Pin_0, LCD1.VDD, Part2.VCC
  N11: LED1.cathode, R3.Pin_1

// code stored in the sketch: Water Tank Level Sensor G1.ino
// VCC pin to 5v
// GND pin to GND
//Echo pin to Digital 9
//Trig pin to Digital 8
/*
  The circuit:
 * LCD RS pin to digital pin 12
 * LCD Enable pin to digital pin 11
 * LCD D4 pin to digital pin 5
 * LCD D5 pin to digital pin 4
 * LCD D6 pin to digital pin 3
 * LCD D7 pin to digital pin 2
 * LCD R/W pin to ground
 * 10K resistor:
 * ends to +5V and ground
 * wiper to LCD VO pin (pin 3)
 */

#include <NewPing.h>
#include <LiquidCrystal.h>
#include <stdio.h> // for function sprintf


int led = 2;
#define TRIGGER_PIN  8  // Arduino pin tied to trigger pin on the ultrasonic sensor.
#define ECHO_PIN     9  // Arduino pin tied to echo pin on the ultrasonic sensor.
#define MAX_DISTANCE 500 // Maximum distance we want to ping for (in centimeters). Maximum sensor distance is rated at 400-500cm.
#define led 13 //Arduino pin to indicate power state

// initialize the library with the numbers of the interface pins
LiquidCrystal lcd(12, 11, 5, 4, 3, 2);

NewPing sonar(TRIGGER_PIN, ECHO_PIN, MAX_DISTANCE); // NewPing setup of pins and maximum distance.

void setup() {
  Serial.begin(115200); // Open serial monitor at 115200 baud to see ping results.
  pinMode (led, OUTPUT);
   lcd.begin(16, 2);
  // Print a message to the LCD.
  lcd.setCursor(0,0);
  lcd.print("Tank Sensor 1G");
  lcd.setCursor(0,1);
  lcd.print("by D Rutherfurd");
  digitalWrite (led, HIGH);
  delay(6000);
  }

void loop() {
  delay(1000);                      // Wait 50ms between pings (about 20 pings/sec). 29ms should be the shortest delay between pings.
  unsigned int uS = sonar.ping(); // Send ping, get ping time in microseconds (uS).
  Serial.print("Distance Monitored: ");
  Serial.print(uS / US_ROUNDTRIP_CM); // Convert ping time to distance and print result (0 = outside set distance range, no ping echo)
  Serial.println("cm");



  // print the Distance Monitored to the LCD Screen
 int tankValue = (uS / US_ROUNDTRIP_CM);
 int tankTotal = 200;

 //String strOne = ("Distance: " + tankValue);
 int tankBalance = (tankTotal-tankValue) * 100;
 //int tankVolume = tankBalance * 100

  lcd.clear();
  lcd.setCursor(0,0);
  lcd.print("Water Tank: 001");
  lcd.setCursor(0,1);
  //lcd.print("Distance: ")
  lcd.print(tankBalance);
  lcd.print(" litres");
}
