# Fritzing sketch scheem (saved by Fritzing 0.9.8b)
breadboards: 1

parts:
  M5 = DC Mini Metal Gear Motor
  M6 = DC Mini Metal Gear Motor
  U1 = L9110 H-bridge module [part_number="L9110 H-bridge"]
  J1 = Basic Servo  # not connected
  J2 = Basic Servo  # not connected
  VALVE1 = Plastic Solenoid Valve  # not connected
  A1 = yf-s401 flow sensor [package=THT]  # not connected
  M7 = DC Mini Metal Gear Motor
  M8 = DC Mini Metal Gear Motor
  U2 = L9110 H-bridge module [part_number="L9110 H-bridge"]
  J3 = Basic Servo  # not connected
  J4 = Basic Servo  # not connected
  VALVE2 = Plastic Solenoid Valve  # not connected
  Компонент1 = Arduino Uno (Rev3) - ICSP

nets:
  N1: M5.IN1, U1.MOTOR_B-B
  N2: M5.IN2, U1.MOTOR_B-A
  N3: M6.IN1, U1.MOTOR_A-B
  N4: M6.IN2, U1.MOTOR_A-A
  N5: U1.B-IA, U1.A-IB, Компонент1.D2
  N6: U1.B-IB, U1.A-IA, Компонент1.D3_PWM
  GND: U1.GND, U2.GND, Компонент1.GND
  VCC: U1.VCC, U2.VCC, Компонент1.5V
  N7: M7.IN1, U2.MOTOR_A-B
  N8: M7.IN2, U2.MOTOR_A-A
  N9: M8.IN1, U2.MOTOR_B-B
  N10: M8.IN2, U2.MOTOR_B-A
  N11: U2.B-IA, U2.A-IB, Компонент1.D4
  N12: U2.B-IB, U2.A-IA, Компонент1.D5_PWM

custom parts:
  yf-s401 flow sensor: Flow sensors sit in line with your water line, and uses a pinwheel sensor to measure how much liquid has moved through it.
