# Fritzing sketch scheme (saved by Fritzing 0.9.8b)
breadboards: 1

parts:
  M5 = DC Mini Metal Gear Motor
  M6 = DC Mini Metal Gear Motor
  U1 = L9110 H-bridge module [part_number="L9110 H-bridge"]
  J1 = Basic Servo
  J2 = Basic Servo
  VALVE1 = Plastic Solenoid Valve
  A1 = yf-s401 flow sensor [package=THT]
  M7 = DC Mini Metal Gear Motor
  M8 = DC Mini Metal Gear Motor
  U2 = L9110 H-bridge module [part_number="L9110 H-bridge"]
  J3 = Basic Servo
  Компонент1 = Arduino Uno (Rev3) - ICSP
  J4 = Basic Servo
  M9 = 1 chan 5v relay module
  VALVE2 = Plastic Solenoid Valve
  M10 = 1 chan 5v relay module
  Power_plug1 = Power plug
  LCD1 = TFT 1.8 inch 160x128 no SD
  Water_Level_Sensor1 = Water Level Sensor

nets:
  N1: M5.IN1, U1.MOTOR_B-B
  N2: M5.IN2, U1.MOTOR_B-A
  N3: M6.IN1, U1.MOTOR_A-B
  N4: M6.IN2, U1.MOTOR_A-A
  N5: U1.B-IA, U1.A-IB, Компонент1.D2
  N6: U1.B-IB, U1.A-IA, Компонент1.D3_PWM
  GND: U1.GND, J1.gnd, J2.gnd, A1.pin2, U2.GND, J3.gnd, Компонент1.GND, J4.gnd, M9.pin_2, M10.pin_2, LCD1.pin2, Water_Level_Sensor1.GND
  VCC: U1.VCC, J1.vcc, J2.vcc, A1.pin1, U2.VCC, J3.vcc, Компонент1.5V, J4.vcc, M9.pin_1, M10.pin_1, LCD1.pin_1, Water_Level_Sensor1.VCC
  N7: J1.pulse, Компонент1.D6_PWM
  N8: J2.pulse, Компонент1.D7
  N9: VALVE1.no_name_yet#1, VALVE2.no_name_yet#1, Power_plug1.VCC
  N10: VALVE1.no_name_yet#2, M9.pin_4
  N11: A1.pin3, Компонент1.A0
  N12: M7.IN1, U2.MOTOR_A-B
  N13: M7.IN2, U2.MOTOR_A-A
  N14: M8.IN1, U2.MOTOR_B-B
  N15: M8.IN2, U2.MOTOR_B-A
  N16: U2.B-IA, U2.A-IB, Компонент1.A5/SCL
  N17: U2.B-IB, U2.A-IA, Компонент1.A4/SDA
  N18: J3.pulse, Компонент1.D5_PWM
  N19: Компонент1.A1, M9.pin_3
  N20: Компонент1.A2, M10.pin_3
  N21: Компонент1.A3, Water_Level_Sensor1.SIG
  N22: Компонент1.ICSP_MISO, Компонент1.D12/MISO, LCD1.pin_7
  N23: Компонент1.D8, LCD1.pin_6
  N24: Компонент1.D9_PWM, LCD1.pin_5
  N25: Компонент1.D10_PWM/SS, LCD1.pin3
  N26: Компонент1.D11_PWM/MOSI, LCD1.pin4
  N27: Компонент1.D4, J4.pulse
  N28: M9.pin_5, M10.pin_5, Power_plug1.GND
  N29: VALVE2.no_name_yet#2, M10.pin_4

notes:
  ПИТАНИЕ
  12 ВОЛЬТ

custom parts:
  yf-s401 flow sensor: Flow sensors sit in line with your water line, and uses a pinwheel sensor to measure how much liquid has moved through it.
  1 chan 5v relay module: 1 Channel 5V Relay Module Board Shield with Optocoupler Support High and Low Level Trigger for Arduino.
  TFT 1.8 inch 160x128 no SD: This is a generic 1.8 tft spi lcd display available on ebay and others. The 1.8" display has 128x160 color pixels and in this version pin names in breadboard (unlike the real board) and with no SD interface.
  Water Level Sensor: A water level sensor. This sensor operates at 3V to 5V. The Sig (signal) pin outputs an analogue signal that is in proportion to the amount of water in contact with the sensor.
