# Fritzing sketch scheme_mega (saved by Fritzing 0.9.10b)
breadboards: 1

parts:
  Компонент1 = Arduino Mega 2560 (Rev3)
  Mod1 = KY-019 5V Relay Module [package="Breakout board"]
  Mod2 = KY-019 5V Relay Module [package="Breakout board"]
  Mod3 = KY-019 5V Relay Module [package="Breakout board"]

nets:
  N1: Компонент1.5V, Mod1.+, Mod2.+, Mod3.+
  N2: Компонент1.D23, Mod3.S
  N3: Компонент1.D25, Mod1.S
  N4: Компонент1.D27, Mod2.S
  N5: Компонент1.GND, Mod1.-, Mod2.-, Mod3.-

custom parts:
  KY-019 5V Relay Module: KY-019 5V Relay module, used to control AC circuits. (Special thanks to vanepp for fixing the PCB holes and other errors)
